// Digital circuit cpu_project.dig as structural Verilog
module cpu_project (
  input  [7:0] M,
  input  [7:0] N,
  input  [13:0] progIn,
  input  reset,
  input  progLoad,
  input  start,
  input  result,
  input  clk,
  output valid,
  output done,
  output [7:0] \output 
);

  wire accA_we, accA_we_exec, accA_we_gcd, accA_we_pre, accB_we, accB_we_exec, branch_taken, cmp_eq, cmp_gr,
       cmp_ls, ctrl_accB_src, ctrl_call_data, ctrl_mem_we, ctrl_not_ssum, ctrl_pram_read_op, ctrl_regC_src,
       ctrl_ret, ctrl_ssum, dest_is_accA, dest_is_accB, dest_is_regC, dest_is_regD, done_clr, done_in,
       done_we, dump_active, dump_active_in, dump_active_we, dump_clr, dump_cnt_is_15, dump_cnt_is_16,
       dump_trigger, eq_in, eq_next_pre, fib_done, fib_i_we, fib_init, fib_n_eq_0, fib_n_eq_1, fib_n_le_1,
       fib_res_init_we, fib_res_loop_we, fib_res_we, flag_eq, flag_gr, flag_ls, flag_we, flag_we_exec,
       flag_we_is_zero, flag_we_nonzero, gcd_a_gt_b, gcd_a_we, gcd_b_gt_a, gcd_b_we, gcd_done, gcd_init,
       gcd_step_a, gcd_step_b, gr_in, gr_next_pre, is_exec_pram_read, ls_in, ls_next_pre, not_reset_done,
       pc_en, pc_en_exec, pc_en_gcd, pc_en_pre, pc_reg_we, prime_out, regC_we, regC_we_exec,
       regD_dec_is_zero, regD_dec_not_zero, regD_we, regD_we_exec, reset_active, reset_clearing,
       reset_or_start, reset_start_load, rram_we, rram_we_exec, rram_we_run, s5_done, sp_is_zero,
       sp_op_is_zero, sp_op_nonzero, sp_we, sp_we_exec, special0_nossum, special_op_is_0, special_op_is_1,
       special_op_is_2, special_op_is_3, ssum_init, ssum_last, ssum_mode, ssum_run, ssum_we, state_is_exec,
       state_is_fetch, state_is_fib_loop, state_is_fib_w, state_is_fib_wa, state_is_fib_wb, state_is_gcd,
       state_is_halt, state_is_idle, stop_executed, valid_in, valid_we;
  wire [1:0] ctrl_flag_we, ctrl_mem_addr_src, ctrl_regD_src, ctrl_sp_op, ctrl_special_op;
  wire [2:0] ctrl_accA_src, ctrl_branch_type, ctrl_reg_dest, fib_start_state, next_state, next_state_exec,
       next_state_exec_base, next_state_fib_loop, next_state_gcd, next_state_pre, next_state_raw,
       ssum_entry_state, state;
  wire [3:0] dump_addr_8, reset_addr_8;
  wire [4:0] fib_i, fib_i_in, fib_i_next, fib_n;
  wire [4:4] dump_cnt, reset_cnt_5;
  wire [7:0] accA, accA_exec_next, accA_in, accA_next, accB, accB_in, accB_next, alu_add, alu_and, alu_div,
       alu_mod, alu_mul, alu_not, alu_or, alu_out, alu_rol, alu_ror, alu_sll, alu_srl, alu_sub, alu_xor,
       gcd_a, gcd_a_in, gcd_a_minus_b, gcd_b, gcd_b_in, gcd_b_minus_a, load_addr, next_PC, next_PC_base, PC,
       pc_in, pc_plus_1, pram_addr, pram_addr_run, regC, regC_in, regC_next, regD, regD_in, regD_minus_1,
       regD_next, rram_addr, rram_addr_cpu, rram_addr_cpu_base, rram_addr_exec, rram_addr_fib,
       rram_addr_fib_base, rram_addr_run, rram_din, rram_din_fib, rram_din_fib_base, rram_din_run,
       rram_din_run_base, SP, sp_in, sp_minus_1, sp_next, sp_plus_1, ssum_addr, ssum_addr_in,
       ssum_addr_plus1, ssum_wr_addr, ssum_wr_data;
  wire [13:0] ir_val, pram_dout;
  wire [15:0] fib_f0, fib_f0_in, fib_f1, fib_f1_in, fib_f_next, fib_res, fib_res_in, fib_res_init, ssum_acc,
       ssum_acc_in, ssum_acc_sum;

  Register #(.Bits(3)) u_STATE (.D(next_state), .C(clk), .en(1'b1), .Q(state));
  Register #(.Bits(8)) u_PC (.D(pc_in), .C(clk), .en(pc_reg_we), .Q(PC));
  Comparator #(.Bits(8)) comparator_1 (.a(regD_minus_1), .b({8{1'b0}}), .eq(regD_dec_is_zero));  // open: gt, lt
  Comparator #(.Bits(2)) comparator_2 (.a(ctrl_special_op), .b(2'b00), .eq(special_op_is_0));  // open: gt, lt
  and and_1 (pc_en_gcd, state_is_gcd, gcd_done);
  and and_2 (is_exec_pram_read, state_is_exec, ctrl_pram_read_op);
  Comparator #(.Bits(2)) comparator_3 (.a(ctrl_special_op), .b(2'b11), .eq(special_op_is_3));  // open: gt, lt
  and and_3 (dump_trigger, valid, result);
  Multiplexer #(.Bits(1)) multiplexer_1 (.sel(done_clr), .in_0(1'b1), .in_1(1'b0), .out(done_in));
  Multiplexer #(.Bits(8)) multiplexer_2 (.sel(ctrl_ret), .in_0(next_PC_base), .in_1(\output ), .out(next_PC));
  and and_4 (ssum_init, state_is_exec, ctrl_ssum);
  Comparator #(.Bits(8)) comparator_4 (.a(SP), .b({8{1'b0}}), .eq(sp_is_zero));  // open: gt, lt
  Add #(.Bits(8)) add_1 (.a(ssum_addr), .b(8'h1), .c_i(1'b0), .s(ssum_addr_plus1));  // open: c_o
  Multiplexer #(.Bits(8)) multiplexer_3 (.sel(state_is_fib_wb), .in_0(8'hc), .in_1(8'hd), .out(ssum_wr_addr));
  Multiplexer #(.Bits(1)) multiplexer_4 (.sel(reset_start_load), .in_0(1'b1), .in_1(1'b0), .out(valid_in));
  Register #(.Bits(14)) IR (.D(pram_dout), .C(clk), .en(state_is_fetch), .Q(ir_val));
  or or_1 (reset_or_start, reset, start);
  Register #(.Bits(1)) reset_active_reg (.D(1'b1), .C(clk), .en(reset), .Q(reset_active));
  Comparator #(.Bits(3)) comparator_5 (.a(state), .b(3'b000), .eq(state_is_idle));  // open: gt, lt
  Comparator #(.Bits(3)) comparator_6 (.a(state), .b(3'b001), .eq(state_is_fetch));  // open: gt, lt
  Comparator #(.Bits(3)) comparator_7 (.a(state), .b(3'b010), .eq(state_is_exec));  // open: gt, lt
  Comparator #(.Bits(3)) comparator_8 (.a(state), .b(3'b011), .eq(state_is_halt));  // open: gt, lt
  Comparator #(.Bits(5)) comparator_9 (
    .a({dump_cnt[4], dump_addr_8}), .b(5'b10000), .eq(dump_cnt_is_16));  // open: gt, lt
  Comparator #(.Bits(5)) comparator_10 (
    .a({dump_cnt[4], dump_addr_8}), .b(5'b01111), .eq(dump_cnt_is_15));  // open: gt, lt
  RAMDualPort #(.AddrBits(8), .Bits(14)) pRAM (
    .A(pram_addr), .Din(progIn), .str(progLoad), .C(clk), .ld(1'b1), .D(pram_dout));
  Multiplexer #(.Bits(8)) multiplexer_5 (.sel(reset_or_start), .in_0(next_PC), .in_1({8{1'b0}}), .out(pc_in));
  and and_5 (pc_en_exec, state_is_exec, special0_nossum);
  Multiplexer #(.Bits(8)) multiplexer_6 (.sel(is_exec_pram_read), .in_0(PC), .in_1(ir_val[7:0]), .out(pram_addr_run));
  or or_2 (dump_active_we, dump_trigger, dump_clr);
  and and_6 (stop_executed, state_is_exec, special_op_is_3);
  Multiplexer #(.Bits(8)) multiplexer_7 (
    .sel(ctrl_call_data), .in_0(rram_din_run_base), .in_1(pc_plus_1), .out(rram_din_run));
  Add #(.Bits(8)) add_2 (.a(PC), .b(8'h1), .c_i(1'b0), .s(pc_plus_1));  // open: c_o
  Register #(.Bits(1)) ssum_mode_reg (.D(ctrl_ssum), .C(clk), .en(state_is_exec), .Q(ssum_mode));
  Multiplexer #(.Bits(3)) multiplexer_8 (.sel(sp_is_zero), .in_0(3'b101), .in_1(3'b110), .out(ssum_entry_state));
  Multiplexer #(.Bits(8)) multiplexer_9 (.sel(ssum_init), .in_0(ssum_addr_plus1), .in_1(SP), .out(ssum_addr_in));
  Add #(.Bits(16)) add_3 (.a(ssum_acc), .b({{8{1'b0}}, \output }), .c_i(1'b0), .s(ssum_acc_sum));  // open: c_o
  Multiplexer #(.Bits(8)) multiplexer_10 (
    .sel(ssum_mode), .in_0(rram_addr_fib_base), .in_1(ssum_wr_addr), .out(rram_addr_fib));
  Counter #(.Bits(8)) load_addr_cnt (.en(progLoad), .C(clk), .clr(reset_or_start), .out(load_addr));  // open: ovf
  Counter #(.Bits(5)) reset_cnt (
    .en(reset_clearing), .C(clk), .clr(reset), .out({reset_cnt_5[4], reset_addr_8}));  // open: ovf
  not not_1 (regD_dec_not_zero, regD_dec_is_zero);
  or or_3 (pc_en_pre, pc_en_exec, pc_en_gcd);
  or or_4 (dump_clr, dump_cnt_is_15, reset_start_load);
  or or_5 (done_clr, reset_start_load, dump_trigger);
  RAMDualPort #(.AddrBits(8), .Bits(8)) rRAM (
    .A(rram_addr), .Din(rram_din), .str(rram_we), .C(clk), .ld(1'b1), .D(\output ));
  Multiplexer #(.Bits(8)) multiplexer_11 (.sel(progLoad), .in_0(pram_addr_run), .in_1(load_addr), .out(pram_addr));
  Register #(.Bits(1)) dump_active_reg (.D(dump_active_in), .C(clk), .en(dump_active_we), .Q(dump_active));
  Comparator #(.Bits(5)) comparator_11 (.a(accA[4:0]), .b(5'b00001), .eq(fib_n_eq_1), .lt(fib_n_eq_0));  // open: gt
  Comparator #(.Bits(3)) comparator_12 (.a(state), .b(3'b100), .eq(state_is_gcd));  // open: gt, lt
  Comparator #(.Bits(3)) comparator_13 (.a(state), .b(3'b101), .eq(state_is_fib_loop));  // open: gt, lt
  Comparator #(.Bits(3)) comparator_14 (.a(state), .b(3'b110), .eq(state_is_fib_wa));  // open: gt, lt
  Comparator #(.Bits(3)) comparator_15 (.a(state), .b(3'b111), .eq(state_is_fib_wb));  // open: gt, lt
  or or_6 (valid_we, stop_executed, reset_start_load);
  or or_7 (reset_start_load, reset_or_start, progLoad);
  ROM #(.AddrBits(6), .Bits(26)) rom_1 (
    .A(ir_val[13:8]), .sel(1'b1),
    .D({ctrl_ssum, ctrl_call_data, ctrl_ret, ctrl_special_op, ctrl_flag_we, ctrl_branch_type, ctrl_pram_read_op, ctrl_mem_addr_src, ctrl_mem_we, ctrl_sp_op, ctrl_regD_src, ctrl_regC_src, ctrl_accB_src, ctrl_accA_src, ctrl_reg_dest}));
  Multiplexer #(.Selector_Bits(3), .Bits(1)) multiplexer_12 (
    .sel(ctrl_branch_type), .in_0(1'b0), .in_1(1'b1), .in_2(flag_eq), .in_3(flag_gr), .in_4(flag_ls),
    .in_5(regD_dec_not_zero), .in_6(1'b0), .in_7(1'b0), .out(branch_taken));
  or or_8 (pc_en, pc_en_pre, state_is_fib_wb);
  Multiplexer #(.Bits(1)) multiplexer_13 (.sel(dump_clr), .in_0(1'b1), .in_1(1'b0), .out(dump_active_in));
  or or_9 (done_we, dump_cnt_is_15, done_clr);
  Register #(.Bits(1)) valid_reg (.D(valid_in), .C(clk), .en(valid_we), .Q(valid));
  Counter #(.Bits(5)) u_dump_cnt (
    .en(dump_active), .C(clk), .clr(dump_clr), .out({dump_cnt[4], dump_addr_8}));  // open: ovf
  Seven_Seg_Hex seven_seg_hex_1 (.d(\output [7:4]), .dp(1'b0));
  or or_10 (fib_n_le_1, fib_n_eq_0, fib_n_eq_1);
  Multiplexer #(.Bits(3)) multiplexer_14 (.sel(fib_n_le_1), .in_0(3'b101), .in_1(3'b110), .out(fib_start_state));
  Multiplexer #(.Bits(3)) multiplexer_15 (.sel(gcd_done), .in_0(3'b100), .in_1(3'b001), .out(next_state_gcd));
  Multiplexer #(.Bits(3)) multiplexer_16 (.sel(reset), .in_0(next_state_pre), .in_1(3'b000), .out(next_state));
  and and_7 (ssum_run, state_is_fib_loop, ssum_mode);
  Multiplexer #(.Bits(3)) multiplexer_17 (
    .sel(ctrl_ssum), .in_0(next_state_exec_base), .in_1(ssum_entry_state), .out(next_state_exec));
  Register #(.Bits(8)) ssum_addr_reg (.D(ssum_addr_in), .C(clk), .en(ssum_we), .Q(ssum_addr));
  Multiplexer #(.Bits(16)) multiplexer_18 (.sel(ssum_init), .in_0(ssum_acc_sum), .in_1({16{1'b0}}), .out(ssum_acc_in));
  Multiplexer #(.Bits(8)) multiplexer_19 (
    .sel(state_is_fib_wb), .in_0(ssum_acc[15:8]), .in_1(ssum_acc[7:0]), .out(ssum_wr_data));
  Multiplexer #(.Bits(8)) multiplexer_20 (.sel(branch_taken), .in_0(pc_plus_1), .in_1(ir_val[7:0]), .out(next_PC_base));
  Seven_Seg_Hex seven_seg_hex_2 (.d(\output [3:0]), .dp(1'b0));
  not not_2 (not_reset_done, reset_cnt_5[4]);
  or or_11 (pc_reg_we, pc_en, reset_or_start);
  Register #(.Bits(1)) done_reg (.D(done_in), .C(clk), .en(done_we), .Q(done));
  Multiplexer #(.Selector_Bits(2), .Bits(3)) multiplexer_21 (
    .sel(ctrl_special_op), .in_0(3'b001), .in_1(3'b100), .in_2(fib_start_state), .in_3(3'b011),
    .out(next_state_exec_base));
  Multiplexer #(.Bits(3)) multiplexer_22 (.sel(s5_done), .in_0(3'b101), .in_1(3'b110), .out(next_state_fib_loop));
  and and_8 (reset_clearing, reset_active, not_reset_done);
  or or_12 (ssum_we, ssum_init, ssum_run);
  Comparator #(.Bits(8)) comparator_16 (.a(ssum_addr), .b({8{1'b1}}), .eq(ssum_last));  // open: gt, lt
  Register #(.Bits(16)) ssum_acc_reg (.D(ssum_acc_in), .C(clk), .en(ssum_we), .Q(ssum_acc));
  Multiplexer #(.Bits(8)) multiplexer_23 (
    .sel(ssum_mode), .in_0(rram_din_fib_base), .in_1(ssum_wr_data), .out(rram_din_fib));
  Multiplexer #(.Selector_Bits(3), .Bits(3)) multiplexer_24 (
    .sel(state), .in_0(3'b000), .in_1(3'b010), .in_2(next_state_exec), .in_3(3'b011), .in_4(next_state_gcd),
    .in_5(next_state_fib_loop), .in_6(3'b111), .in_7(3'b001), .out(next_state_raw));
  Multiplexer #(.Bits(3)) multiplexer_25 (.sel(start), .in_0(next_state_raw), .in_1(3'b001), .out(next_state_pre));
  Sub #(.Bits(8)) sub_1 (.a(regD), .b(8'h1), .c_i(1'b0), .s(regD_minus_1));  // open: c_o
  and and_9 (accA_we_gcd, state_is_gcd, gcd_done);
  Sub #(.Bits(8)) sub_2 (.a(SP), .b(8'h1), .c_i(1'b0), .s(sp_minus_1));  // open: c_o
  Add #(.Bits(8)) add_4 (.a(SP), .b(8'h1), .c_i(1'b0), .s(sp_plus_1));  // open: c_o
  Comparator #(.Bits(2)) comparator_17 (.a(ctrl_sp_op), .b(2'b00), .eq(sp_op_is_zero));  // open: gt, lt
  Multiplexer #(.Bits(8)) multiplexer_26 (.sel(ctrl_regC_src), .in_0(accA), .in_1(M), .out(regC_next));
  not not_3 (ctrl_not_ssum, ctrl_ssum);
  Multiplexer #(.Bits(1)) multiplexer_27 (.sel(ssum_mode), .in_0(fib_done), .in_1(ssum_last), .out(s5_done));
  Multiplexer #(.Bits(8)) multiplexer_28 (
    .sel(ssum_run), .in_0(rram_addr_cpu_base), .in_1(ssum_addr), .out(rram_addr_cpu));
  Multiplexer #(.Bits(8)) multiplexer_29 (.sel(ctrl_accB_src), .in_0(ir_val[7:0]), .in_1(accA), .out(accB_next));
  Multiplexer #(.Selector_Bits(2), .Bits(8)) multiplexer_30 (
    .sel(ctrl_mem_addr_src), .in_0(ir_val[7:0]), .in_1(regC), .in_2(sp_minus_1), .in_3(SP),
    .out(rram_addr_exec));
  or or_13 (state_is_fib_w, state_is_fib_wa, state_is_fib_wb);
  Multiplexer #(.Bits(8)) multiplexer_31 (
    .sel(state_is_fib_wb), .in_0(fib_res[15:8]), .in_1(fib_res[7:0]), .out(rram_din_fib_base));
  and and_10 (rram_we_exec, state_is_exec, ctrl_mem_we);
  Comparator #(.Bits(3)) comparator_18 (.a(ctrl_reg_dest), .b(3'b010), .eq(dest_is_accB));  // open: gt, lt
  Comparator #(.Bits(3)) comparator_19 (.a(ctrl_reg_dest), .b(3'b100), .eq(dest_is_regD));  // open: gt, lt
  Multiplexer #(.Selector_Bits(3), .Bits(8)) multiplexer_32 (
    .sel(ctrl_accA_src), .in_0(ir_val[7:0]), .in_1(accB), .in_2(regC), .in_3(regD), .in_4(SP),
    .in_5(\output ), .in_6(pram_dout[7:0]), .in_7(alu_out), .out(accA_exec_next));
  Comparator #(.Bits(3)) comparator_20 (.a(ctrl_reg_dest), .b(3'b001), .eq(dest_is_accA));  // open: gt, lt
  Multiplexer #(.Selector_Bits(2), .Bits(8)) multiplexer_33 (
    .sel(ctrl_sp_op), .in_0(SP), .in_1(sp_minus_1), .in_2(sp_plus_1), .in_3(SP), .out(sp_next));
  not not_4 (sp_op_nonzero, sp_op_is_zero);
  Multiplexer #(.Bits(8)) multiplexer_34 (.sel(reset), .in_0(accB_next), .in_1({8{1'b0}}), .out(accB_in));
  Multiplexer #(.Bits(8)) multiplexer_35 (.sel(reset), .in_0(regC_next), .in_1({8{1'b0}}), .out(regC_in));
  Comparator #(.Bits(3)) comparator_21 (.a(ctrl_reg_dest), .b(3'b011), .eq(dest_is_regC));  // open: gt, lt
  Multiplexer #(.Selector_Bits(2), .Bits(8)) multiplexer_36 (
    .sel(ctrl_regD_src), .in_0(accA), .in_1(N), .in_2(regD_minus_1), .in_3(accA), .out(regD_next));
  Multiplexer #(.Bits(8)) multiplexer_37 (
    .sel(state_is_fib_w), .in_0(rram_addr_exec), .in_1(rram_addr_fib), .out(rram_addr_cpu_base));
  Multiplexer #(.Bits(8)) multiplexer_38 (
    .sel(state_is_fib_w), .in_0(accA), .in_1(rram_din_fib), .out(rram_din_run_base));
  Multiplexer #(.Bits(8)) multiplexer_39 (.sel(state_is_fib_wb), .in_0(8'ha), .in_1(8'hb), .out(rram_addr_fib_base));
  or or_14 (rram_we_run, rram_we_exec, state_is_fib_w);
  and and_11 (accB_we_exec, state_is_exec, dest_is_accB);
  and and_12 (special0_nossum, special_op_is_0, ctrl_not_ssum);
  Multiplexer #(.Bits(8)) multiplexer_40 (.sel(reset_or_start), .in_0(sp_next), .in_1({8{1'b0}}), .out(sp_in));
  Register #(.Bits(8)) u_accB (.D(accB_in), .C(clk), .en(accB_we), .Q(accB));
  Register #(.Bits(8)) u_regC (.D(regC_in), .C(clk), .en(regC_we), .Q(regC));
  Multiplexer #(.Bits(8)) multiplexer_41 (.sel(reset), .in_0(regD_next), .in_1({8{1'b0}}), .out(regD_in));
  and and_13 (regD_we_exec, state_is_exec, dest_is_regD);
  and and_14 (accA_we_exec, state_is_exec, dest_is_accA);
  and and_15 (sp_we_exec, state_is_exec, sp_op_nonzero);
  and and_16 (regC_we_exec, state_is_exec, dest_is_regC);
  Multiplexer #(.Bits(8)) multiplexer_42 (.sel(accA_we_gcd), .in_0(accA_exec_next), .in_1(gcd_a), .out(accA_next));
  Multiplexer #(.Bits(8)) multiplexer_43 (
    .sel(valid), .in_0(rram_addr_cpu), .in_1({4'b0000, dump_addr_8}), .out(rram_addr_run));
  Register #(.Bits(8)) u_SP (.D(sp_in), .C(clk), .en(sp_we), .Q(SP));
  Multiplexer #(.Bits(8)) multiplexer_44 (.sel(reset_clearing), .in_0(rram_din_run), .in_1({8{1'b0}}), .out(rram_din));
  or or_15 (accB_we, accB_we_exec, reset);
  or or_16 (rram_we, rram_we_run, reset_clearing);
  or or_17 (sp_we, sp_we_exec, reset_or_start);
  or or_18 (regC_we, regC_we_exec, reset);
  Register #(.Bits(8)) u_regD (.D(regD_in), .C(clk), .en(regD_we), .Q(regD));
  or or_19 (regD_we, regD_we_exec, reset);
  Multiplexer #(.Bits(8)) multiplexer_45 (.sel(reset), .in_0(accA_next), .in_1({8{1'b0}}), .out(accA_in));
  or or_20 (accA_we_pre, accA_we_exec, accA_we_gcd);
  Multiplexer #(.Bits(8)) multiplexer_46 (
    .sel(reset_clearing), .in_0(rram_addr_run), .in_1({4'b0000, reset_addr_8}), .out(rram_addr));
  Register #(.Bits(8)) u_accA (.D(accA_in), .C(clk), .en(accA_we), .Q(accA));
  or or_21 (accA_we, accA_we_pre, reset);
  Comparator #(.Signed("true"), .Bits(8)) comparator_22 (.a(accA), .b(accB), .gt(cmp_gr), .eq(cmp_eq), .lt(cmp_ls));
  ROM #(.AddrBits(8), .Bits(1)) rom_2 (.A(accA), .sel(1'b1), .D(prime_out));
  Add #(.Bits(8)) add_5 (.a(accA), .b(accB), .c_i(1'b0), .s(alu_add));  // open: c_o
  Sub #(.Bits(8)) sub_3 (.a(accA), .b(accB), .c_i(1'b0), .s(alu_sub));  // open: c_o
  assign alu_and = accA & accB;  // And and_17, 8 bits wide
  assign alu_or = accA | accB;  // Or or_22, 8 bits wide
  assign alu_xor = accA ^ accB;  // XOr xor_1, 8 bits wide
  assign alu_not = ~accA;  // Not not_5, 8 bits wide
  Multiplexer #(.Selector_Bits(2), .Bits(1)) multiplexer_47 (
    .sel(ctrl_flag_we), .in_0(flag_ls), .in_1(cmp_ls), .in_2(flag_ls), .in_3(flag_ls), .out(ls_next_pre));
  Comparator #(.Bits(2)) comparator_23 (.a(ctrl_flag_we), .b(2'b00), .eq(flag_we_is_zero));  // open: gt, lt
  Comparator #(.Bits(8)) comparator_24 (.a(gcd_a), .b(gcd_b), .gt(gcd_a_gt_b), .eq(gcd_done), .lt(gcd_b_gt_a));
  Sub #(.Bits(8)) sub_4 (.a(gcd_a), .b(gcd_b), .c_i(1'b0), .s(gcd_a_minus_b));  // open: c_o
  Multiplexer #(.Bits(8)) multiplexer_48 (.sel(gcd_init), .in_0(gcd_b_minus_a), .in_1(accB), .out(gcd_b_in));
  Sub #(.Bits(8)) sub_5 (.a(gcd_b), .b(gcd_a), .c_i(1'b0), .s(gcd_b_minus_a));  // open: c_o
  Comparator #(.Bits(2)) comparator_25 (.a(ctrl_special_op), .b(2'b01), .eq(special_op_is_1));  // open: gt, lt
  Comparator #(.Bits(2)) comparator_26 (.a(ctrl_special_op), .b(2'b10), .eq(special_op_is_2));  // open: gt, lt
  Add #(.Bits(5)) add_6 (.a(fib_i), .b(5'b00001), .c_i(1'b0), .s(fib_i_next));  // open: c_o
  Comparator #(.Bits(5)) comparator_27 (.a(fib_i_next), .b(fib_n), .eq(fib_done));  // open: gt, lt
  Multiplexer #(.Bits(16)) multiplexer_49 (.sel(fib_init), .in_0(fib_f_next), .in_1(16'h1), .out(fib_f1_in));
  Multiplexer #(.Bits(16)) multiplexer_50 (.sel(fib_n_eq_1), .in_0({16{1'b0}}), .in_1(16'h1), .out(fib_res_init));
  and and_18 (fib_res_loop_we, state_is_fib_loop, fib_done);
  and and_19 (fib_res_init_we, fib_init, fib_n_le_1);
  Add #(.Bits(16)) add_7 (.a(fib_f0), .b(fib_f1), .c_i(1'b0), .s(fib_f_next));  // open: c_o
  BarrelShifter #(.Bits(8)) barrelshifter_1 (.in(accA), .shift({1'b0, accB[2:0]}), .out(alu_sll));
  BarrelShifter #(.Bits(8), .direction("right")) barrelshifter_2 (.in(accA), .shift({1'b0, accB[2:0]}), .out(alu_srl));
  Mul #(.Bits(4)) mul_1 (.a(accA[3:0]), .b(accB[3:0]), .mul(alu_mul));
  Div #(.Bits(8)) div_1 (.a(accA), .b(accB), .q(alu_div), .r(alu_mod));
  Multiplexer #(.Selector_Bits(2), .Bits(1)) multiplexer_51 (
    .sel(ctrl_flag_we), .in_0(flag_eq), .in_1(cmp_eq), .in_2(prime_out), .in_3(flag_eq), .out(eq_next_pre));
  Multiplexer #(.Selector_Bits(2), .Bits(1)) multiplexer_52 (
    .sel(ctrl_flag_we), .in_0(flag_gr), .in_1(cmp_gr), .in_2(flag_gr), .in_3(flag_gr), .out(gr_next_pre));
  Multiplexer #(.Bits(1)) multiplexer_53 (.sel(reset), .in_0(ls_next_pre), .in_1(1'b0), .out(ls_in));
  not not_6 (flag_we_nonzero, flag_we_is_zero);
  Multiplexer #(.Bits(8)) multiplexer_54 (.sel(gcd_init), .in_0(gcd_a_minus_b), .in_1(accA), .out(gcd_a_in));
  and and_20 (gcd_step_a, state_is_gcd, gcd_a_gt_b);
  Register #(.Bits(8)) u_gcd_b (.D(gcd_b_in), .C(clk), .en(gcd_b_we), .Q(gcd_b));
  and and_21 (gcd_step_b, state_is_gcd, gcd_b_gt_a);
  and and_22 (gcd_init, state_is_exec, special_op_is_1);
  Register #(.Bits(16)) u_fib_f1 (.D(fib_f1_in), .C(clk), .en(fib_i_we), .Q(fib_f1));
  Multiplexer #(.Bits(16)) multiplexer_55 (.sel(fib_init), .in_0(fib_f_next), .in_1(fib_res_init), .out(fib_res_in));
  Multiplexer #(.Bits(5)) multiplexer_56 (.sel(fib_init), .in_0(fib_i_next), .in_1(5'b00001), .out(fib_i_in));
  Multiplexer #(.Bits(16)) multiplexer_57 (.sel(fib_init), .in_0(fib_f1), .in_1({16{1'b0}}), .out(fib_f0_in));
  and and_23 (fib_init, state_is_exec, special_op_is_2);
  or or_23 (fib_res_we, fib_res_loop_we, fib_res_init_we);
  BarrelShifter #(.Bits(8), .barrelShifterMode("rotate")) barrelshifter_3 (
    .in(accA), .shift({1'b0, accB[2:0]}), .out(alu_rol));
  BarrelShifter #(.Bits(8), .barrelShifterMode("rotate"), .direction("right")) barrelshifter_4 (
    .in(accA), .shift({1'b0, accB[2:0]}), .out(alu_ror));
  Multiplexer #(.Bits(1)) multiplexer_58 (.sel(reset), .in_0(eq_next_pre), .in_1(1'b0), .out(eq_in));
  Multiplexer #(.Bits(1)) multiplexer_59 (.sel(reset), .in_0(gr_next_pre), .in_1(1'b0), .out(gr_in));
  Register #(.Bits(1)) ls (.D(ls_in), .C(clk), .en(flag_we), .Q(flag_ls));
  and and_24 (flag_we_exec, state_is_exec, flag_we_nonzero);
  Register #(.Bits(16)) u_fib_res (.D(fib_res_in), .C(clk), .en(fib_res_we), .Q(fib_res));
  Register #(.Bits(8)) u_gcd_a (.D(gcd_a_in), .C(clk), .en(gcd_a_we), .Q(gcd_a));
  or or_24 (gcd_a_we, gcd_init, gcd_step_a);
  or or_25 (gcd_b_we, gcd_init, gcd_step_b);
  or or_26 (fib_i_we, fib_init, state_is_fib_loop);
  Register #(.Bits(5)) u_fib_n (.D(accA[4:0]), .C(clk), .en(fib_init), .Q(fib_n));
  Register #(.Bits(16)) u_fib_f0 (.D(fib_f0_in), .C(clk), .en(fib_i_we), .Q(fib_f0));
  Register #(.Bits(1)) eq (.D(eq_in), .C(clk), .en(flag_we), .Q(flag_eq));
  Register #(.Bits(1)) gr (.D(gr_in), .C(clk), .en(flag_we), .Q(flag_gr));
  or or_27 (flag_we, flag_we_exec, reset);
  Register #(.Bits(5)) u_fib_i (.D(fib_i_in), .C(clk), .en(fib_i_we), .Q(fib_i));
  Multiplexer #(.Selector_Bits(4), .Bits(8)) multiplexer_60 (
    .sel(ir_val[11:8]), .in_0(alu_add), .in_1(alu_sub), .in_2(alu_mul), .in_3({8{1'b0}}), .in_4(alu_div),
    .in_5(alu_mod), .in_6({8{1'b0}}), .in_7({8{1'b0}}), .in_8(alu_and), .in_9(alu_or), .in_10(alu_xor),
    .in_11(alu_not), .in_12(alu_sll), .in_13(alu_srl), .in_14(alu_rol), .in_15(alu_ror), .out(alu_out));

  // Other names for the same wires on the sheet: accA_lo4[3:0] = accA[3:0]; accA_lo5[4:0] = accA[4:0];
  //   accA_hi4[3:0] = accA[7:4]; accA_hi3[2:0] = accA[7:5]; accB_lo3[2:0] = accB[2:0]; accB_lo4[3:0] = accB[3:0];
  //   shift_amt_4[2:0] = accB[2:0]; accB_bit3 = accB[3]; accB_hi4[3:0] = accB[7:4];
  //   ctrl_word[25:0] = {ctrl_ssum, ctrl_call_data, ctrl_ret, ctrl_special_op, ctrl_flag_we, ctrl_branch_type, ctrl_pram_read_op, ctrl_mem_addr_src, ctrl_mem_we, ctrl_sp_op, ctrl_regD_src, ctrl_regC_src, ctrl_accB_src, ctrl_accA_src, ctrl_reg_dest};
  //   dump_cnt[3:0] = dump_addr_8; dump_cnt_lo4[3:0] = dump_addr_8; dump_cnt_hi1 = dump_cnt[4];
  //   fib_res_lo8[7:0] = fib_res[7:0]; fib_res_hi8[7:0] = fib_res[15:8]; operand[7:0] = ir_val[7:0];
  //   opcode[5:0] = ir_val[13:8]; opcode_lo4[3:0] = ir_val[11:8]; opcode_hi2[1:0] = ir_val[13:12];
  //   ssum_rd16[7:0] = \output ; pram_dout_lo8[7:0] = pram_dout[7:0]; pram_dout_hi6[5:0] = pram_dout[13:8];
  //   reset_cnt_4[3:0] = reset_addr_8; reset_cnt_5[3:0] = reset_addr_8; reset_done_flag = reset_cnt_5[4];
  //   ssum_acc_lo8[7:0] = ssum_acc[7:0]; ssum_acc_hi8[7:0] = ssum_acc[15:8]

  // Notes on the sheet:
  //   GLOBAL CONSTANTS
  //   2. INSTRUCTION REGISTER & CONTROL DECODER
  //   3. FINITE STATE MACHINE (FSM)
  //   4. PROGRAM COUNTER (PC) & BRANCH LOGIC
  //   5. OUTPUT DUMPER & STATUS (valid, done)
  //   SECRET: CALL / RET (data = PC+1, PC <- rRAM[SP])
  //   SECRET: SSUM control, entry, exit (reuses FSM states S5 S6 S7)
  //   SECRET: SSUM next-state and last-address check
  //   SECRET: SSUM address counter
  //   SECRET: SSUM 16-bit accumulator
  //   SECRET: SSUM result write rRAM[0x0C:0x0D] and address/data muxes
  //   SECRET: constants
  //   1. RESET & PROG_LOAD CONTROLLER
  //   contents of rom_1 (hex, n*v repeats v):
  //   0,1,2,0,9,42,3,4,11,19,21,0,83,104,0,0,29,1000,8031,0,2029,3000
  //   ,0,0,5400,6829,0,0,1015400,806800,0,0,16*39,10000,20000,30000
  //   ,40000,50204,0,0,0,80000,100000,0,0,200000,400000,2000000,600000
  //   6. REGISTER FILE (SP, B, C, D, A)
  //   7. MEMORY (rRAM) ARBITRATION (addr, din, we)
  //   8. ARITHMETIC LOGIC UNIT (ALU)
  //   9. FLAGS & COMPARATOR / ISPRIME
  //   10. HARDWARE GCD SUBSYSTEM
  //   11. HARDWARE FIBONACCI SUBSYSTEM
  //   contents of rom_2 (hex, n*v repeats v):
  //   0,0,1,1,0,1,0,1,0,0,0,1,0,1,0,0,0,1,0,1,0,0,0,1,5*0,1,0,1,5*0
  //   ,1,0,0,0,1,0,1,0,0,0,1,5*0,1,5*0,1,0,1,5*0,1,0,0,0,1,0,1,5*0,1
  //   ,0,0,0,1,5*0,1,7*0,1,0,0,0,1,0,1,0,0,0,1,0,1,0,0,0,1,13*0,1,0,0,0
  //   ,1,5*0,1,0,1,9*0,1,0,1,5*0,1,5*0,1,0,0,0,1,5*0,1,5*0,1,0,1,9*0
  //   ,1,0,1,0,0,0,1,0,1,11*0,1,11*0,1,0,0,0,1,0,1,0,0,0,1,5*0,1,0,1
  //   ,9*0,1
endmodule

/* Test case 25_P12T02:
M N progIn reset progLoad start result clk valid done output
0 0 0 0 0 0 0 C x x x
0 0 0 1 0 0 0 C 0 0 x
repeat(20) 0 0 0 0 0 0 0 C 0 x x
0 0 511 0 1 0 0 C 0 x x
0 0 513 0 1 0 0 C 0 x x
0 0 15360 0 1 0 0 C 0 x x
0 0 4352 0 1 0 0 C 0 x x
0 0 257 0 1 0 0 C 0 x x
0 0 767 0 1 0 0 C 0 x x
0 0 15360 0 1 0 0 C 0 x x
0 0 4353 0 1 0 0 C 0 x x
0 0 384 0 1 0 0 C 0 x x
0 0 608 0 1 0 0 C 0 x x
0 0 15360 0 1 0 0 C 0 x x
0 0 4354 0 1 0 0 C 0 x x
0 0 477 0 1 0 0 C 0 x x
0 0 529 0 1 0 0 C 0 x x
0 0 15360 0 1 0 0 C 0 x x
0 0 4355 0 1 0 0 C 0 x x
0 0 506 0 1 0 0 C 0 x x
0 0 757 0 1 0 0 C 0 x x
0 0 15360 0 1 0 0 C 0 x x
0 0 4356 0 1 0 0 C 0 x x
0 0 1024 0 1 0 0 C 0 x x
0 0 4367 0 1 0 0 C 0 x x
0 0 16128 0 1 0 0 C 0 x x
0 0 0 0 0 1 0 C x 0 x
repeat(1821) 0 0 0 0 0 0 0 C x 0 x
0 0 0 0 0 0 0 C 1 0 x
0 0 0 0 0 0 1 C 1 0 1
0 0 0 0 0 0 0 C 1 0 1
0 0 0 0 0 0 0 C 1 0 32
0 0 0 0 0 0 0 C 1 0 17
0 0 0 0 0 0 0 C 1 0 5
repeat(10) 0 0 0 0 0 0 0 C 1 0 0
0 0 0 0 0 0 0 C 1 0 245
repeat(2) 0 0 0 0 0 0 0 C 1 1 x
*/

/* Test case 22_P09T02:
M N progIn reset progLoad start result clk valid done output
0 0 0 0 0 0 0 C x x x
0 0 0 1 0 0 0 C 0 0 x
repeat(20) 0 0 0 0 0 0 0 C 0 x x
0 0 435 0 1 0 0 C 0 x x
0 0 515 0 1 0 0 C 0 x x
0 0 11264 0 1 0 0 C 0 x x
0 0 4352 0 1 0 0 C 0 x x
0 0 435 0 1 0 0 C 0 x x
0 0 515 0 1 0 0 C 0 x x
0 0 11520 0 1 0 0 C 0 x x
0 0 4353 0 1 0 0 C 0 x x
0 0 435 0 1 0 0 C 0 x x
0 0 515 0 1 0 0 C 0 x x
0 0 11776 0 1 0 0 C 0 x x
0 0 4354 0 1 0 0 C 0 x x
0 0 435 0 1 0 0 C 0 x x
0 0 515 0 1 0 0 C 0 x x
0 0 12032 0 1 0 0 C 0 x x
0 0 4355 0 1 0 0 C 0 x x
0 0 435 0 1 0 0 C 0 x x
0 0 512 0 1 0 0 C 0 x x
0 0 11264 0 1 0 0 C 0 x x
0 0 4356 0 1 0 0 C 0 x x
0 0 435 0 1 0 0 C 0 x x
0 0 519 0 1 0 0 C 0 x x
0 0 12032 0 1 0 0 C 0 x x
0 0 4357 0 1 0 0 C 0 x x
0 0 435 0 1 0 0 C 0 x x
0 0 521 0 1 0 0 C 0 x x
0 0 11776 0 1 0 0 C 0 x x
0 0 4358 0 1 0 0 C 0 x x
0 0 435 0 1 0 0 C 0 x x
0 0 767 0 1 0 0 C 0 x x
0 0 11520 0 1 0 0 C 0 x x
0 0 4359 0 1 0 0 C 0 x x
0 0 16128 0 1 0 0 C 0 x x
0 0 0 0 0 1 0 C x 0 x
repeat(135) 0 0 0 0 0 0 0 C x 0 x
0 0 0 0 0 0 0 C 1 0 x
0 0 0 0 0 0 1 C 1 0 152
0 0 0 0 0 0 0 C 1 0 22
0 0 0 0 0 0 0 C 1 0 157
0 0 0 0 0 0 0 C 1 0 118
0 0 0 0 0 0 0 C 1 0 179
repeat(2) 0 0 0 0 0 0 0 C 1 0 103
0 0 0 0 0 0 0 C 1 0 1
repeat(8) 0 0 0 0 0 0 0 C 1 0 0
repeat(2) 0 0 0 0 0 0 0 C 1 1 x
*/

/* Test case 19_P06T02:
M N progIn reset progLoad start result clk valid done output
0 0 0 0 0 0 0 C x x x
0 0 0 1 0 0 0 C 0 0 x
repeat(20) 0 0 0 0 0 0 0 C 0 x x
0 0 3072 0 1 0 0 C 0 x x
0 0 3328 0 1 0 0 C 0 x x
0 0 2048 0 1 0 0 C 0 x x
0 0 4352 0 1 0 0 C 0 x x
0 0 2304 0 1 0 0 C 0 x x
0 0 4353 0 1 0 0 C 0 x x
0 0 2048 0 1 0 0 C 0 x x
0 0 1280 0 1 0 0 C 0 x x
0 0 2304 0 1 0 0 C 0 x x
0 0 8192 0 1 0 0 C 0 x x
0 0 4354 0 1 0 0 C 0 x x
0 0 16128 0 1 0 0 C 0 x x
3 4 0 0 0 1 0 C x 0 x
repeat(51) 3 4 0 0 0 0 0 C x 0 x
3 4 0 0 0 0 0 C 1 0 x
3 4 0 0 0 0 1 C 1 0 3
3 4 0 0 0 0 0 C 1 0 4
3 4 0 0 0 0 0 C 1 0 7
repeat(13) 3 4 0 0 0 0 0 C 1 0 0
repeat(2) 3 4 0 0 0 0 0 C 1 1 x
128 127 0 0 0 1 0 C x 0 x
repeat(51) 128 127 0 0 0 0 0 C x 0 x
128 127 0 0 0 0 0 C 1 0 x
128 127 0 0 0 0 1 C 1 0 128
128 127 0 0 0 0 0 C 1 0 127
128 127 0 0 0 0 0 C 1 0 255
repeat(13) 128 127 0 0 0 0 0 C 1 0 0
repeat(2) 128 127 0 0 0 0 0 C 1 1 x
*/

/* Test case 16_P03T02:
M N progIn reset progLoad start result clk valid done output
0 0 0 0 0 0 0 C x x x
0 0 0 1 0 0 0 C 0 0 x
repeat(20) 0 0 0 0 0 0 0 C 0 x x
0 0 4628 0 1 0 0 C 0 x x
0 0 4352 0 1 0 0 C 0 x x
0 0 4629 0 1 0 0 C 0 x x
0 0 4353 0 1 0 0 C 0 x x
0 0 4630 0 1 0 0 C 0 x x
0 0 4354 0 1 0 0 C 0 x x
0 0 4631 0 1 0 0 C 0 x x
0 0 4355 0 1 0 0 C 0 x x
0 0 4632 0 1 0 0 C 0 x x
0 0 4356 0 1 0 0 C 0 x x
0 0 4633 0 1 0 0 C 0 x x
0 0 4357 0 1 0 0 C 0 x x
0 0 4634 0 1 0 0 C 0 x x
0 0 4358 0 1 0 0 C 0 x x
0 0 4635 0 1 0 0 C 0 x x
0 0 4359 0 1 0 0 C 0 x x
0 0 16128 0 1 0 0 C 0 x x
repeat(3) 0 0 0 0 1 0 0 C 0 x x
0 0 16188 0 1 0 0 C 0 x x
0 0 16257 0 1 0 0 C 0 x x
0 0 16143 0 1 0 0 C 0 x x
0 0 16368 0 1 0 0 C 0 x x
0 0 16213 0 1 0 0 C 0 x x
0 0 16298 0 1 0 0 C 0 x x
0 0 16146 0 1 0 0 C 0 x x
0 0 16180 0 1 0 0 C 0 x x
0 0 0 0 0 1 0 C x 0 x
repeat(71) 0 0 0 0 0 0 0 C x 0 x
0 0 0 0 0 0 0 C 1 0 x
0 0 0 0 0 0 1 C 1 0 60
0 0 0 0 0 0 0 C 1 0 129
0 0 0 0 0 0 0 C 1 0 15
0 0 0 0 0 0 0 C 1 0 240
0 0 0 0 0 0 0 C 1 0 85
0 0 0 0 0 0 0 C 1 0 170
0 0 0 0 0 0 0 C 1 0 18
0 0 0 0 0 0 0 C 1 0 52
repeat(8) 0 0 0 0 0 0 0 C 1 0 0
repeat(2) 0 0 0 0 0 0 0 C 1 1 x
*/

/* Test case 12_P12T01:
M N progIn reset progLoad start result clk valid done output
0 0 0 0 0 0 0 0 x x x
0 0 0 0 0 0 0 1 x x x
0 0 0 1 0 0 0 0 x x x
0 0 0 1 0 0 0 1 0 0 x
0 0 0 0 0 0 0 0 0 x x
0 0 0 0 0 0 0 1 0 x x
0 0 0 0 0 0 0 0 0 x x
0 0 0 0 0 0 0 1 0 x x
0 0 0 0 0 0 0 0 0 x x
0 0 0 0 0 0 0 1 0 x x
0 0 0 0 0 0 0 0 0 x x
0 0 0 0 0 0 0 1 0 x x
0 0 0 0 0 0 0 0 0 x x
0 0 0 0 0 0 0 1 0 x x
0 0 0 0 0 0 0 0 0 x x
0 0 0 0 0 0 0 1 0 x x
0 0 0 0 0 0 0 0 0 x x
0 0 0 0 0 0 0 1 0 x x
0 0 0 0 0 0 0 0 0 x x
0 0 0 0 0 0 0 1 0 x x
0 0 0 0 0 0 0 0 0 x x
0 0 0 0 0 0 0 1 0 x x
0 0 0 0 0 0 0 0 0 x x
0 0 0 0 0 0 0 1 0 x x
0 0 0 0 0 0 0 0 0 x x
0 0 0 0 0 0 0 1 0 x x
0 0 0 0 0 0 0 0 0 x x
0 0 0 0 0 0 0 1 0 x x
0 0 0 0 0 0 0 0 0 x x
0 0 0 0 0 0 0 1 0 x x
0 0 0 0 0 0 0 0 0 x x
0 0 0 0 0 0 0 1 0 x x
0 0 0 0 0 0 0 0 0 x x
0 0 0 0 0 0 0 1 0 x x
0 0 0 0 0 0 0 0 0 x x
0 0 0 0 0 0 0 1 0 x x
0 0 0 0 0 0 0 0 0 x x
0 0 0 0 0 0 0 1 0 x x
0 0 0 0 0 0 0 0 0 x x
0 0 0 0 0 0 0 1 0 x x
0 0 0 0 0 0 0 0 0 x x
0 0 0 0 0 0 0 1 0 x x
0 0 0 0 0 0 0 0 0 x x
0 0 0 0 0 0 0 1 0 x x
0 0 268 0 1 0 0 0 0 x x
0 0 268 0 1 0 0 1 0 x x
0 0 530 0 1 0 0 0 0 x x
0 0 530 0 1 0 0 1 0 x x
0 0 15360 0 1 0 0 0 0 x x
0 0 15360 0 1 0 0 1 0 x x
0 0 4352 0 1 0 0 0 0 x x
0 0 4352 0 1 0 0 1 0 x x
0 0 356 0 1 0 0 0 0 x x
0 0 356 0 1 0 0 1 0 x x
0 0 587 0 1 0 0 0 0 x x
0 0 587 0 1 0 0 1 0 x x
0 0 15360 0 1 0 0 0 0 x x
0 0 15360 0 1 0 0 1 0 x x
0 0 4353 0 1 0 0 0 0 x x
0 0 4353 0 1 0 0 1 0 x x
0 0 273 0 1 0 0 0 0 x x
0 0 273 0 1 0 0 1 0 x x
0 0 517 0 1 0 0 0 0 x x
0 0 517 0 1 0 0 1 0 x x
0 0 15360 0 1 0 0 0 0 x x
0 0 15360 0 1 0 0 1 0 x x
0 0 4354 0 1 0 0 0 0 x x
0 0 4354 0 1 0 0 1 0 x x
0 0 304 0 1 0 0 0 0 x x
0 0 304 0 1 0 0 1 0 x x
0 0 560 0 1 0 0 0 0 x x
0 0 560 0 1 0 0 1 0 x x
0 0 15360 0 1 0 0 0 0 x x
0 0 15360 0 1 0 0 1 0 x x
0 0 4355 0 1 0 0 0 0 x x
0 0 4355 0 1 0 0 1 0 x x
0 0 1024 0 1 0 0 0 0 x x
0 0 1024 0 1 0 0 1 0 x x
0 0 4367 0 1 0 0 0 0 x x
0 0 4367 0 1 0 0 1 0 x x
0 0 16128 0 1 0 0 0 0 x x
0 0 16128 0 1 0 0 1 0 x x
0 0 0 0 0 1 0 0 x x x
0 0 0 0 0 1 0 1 x 0 x
0 0 0 0 0 0 0 0 x 0 x
0 0 0 0 0 0 0 1 x 0 x
0 0 0 0 0 0 0 0 x 0 x
0 0 0 0 0 0 0 1 x 0 x
0 0 0 0 0 0 0 0 x 0 x
0 0 0 0 0 0 0 1 x 0 x
0 0 0 0 0 0 0 0 x 0 x
0 0 0 0 0 0 0 1 x 0 x
0 0 0 0 0 0 0 0 x 0 x
0 0 0 0 0 0 0 1 x 0 x
0 0 0 0 0 0 0 0 x 0 x
0 0 0 0 0 0 0 1 x 0 x
0 0 0 0 0 0 0 0 x 0 x
0 0 0 0 0 0 0 1 x 0 x
0 0 0 0 0 0 0 0 x 0 x
0 0 0 0 0 0 0 1 x 0 x
0 0 0 0 0 0 0 0 x 0 x
0 0 0 0 0 0 0 1 x 0 x
0 0 0 0 0 0 0 0 x 0 x
0 0 0 0 0 0 0 1 x 0 x
0 0 0 0 0 0 0 0 x 0 x
0 0 0 0 0 0 0 1 x 0 x
0 0 0 0 0 0 0 0 x 0 x
0 0 0 0 0 0 0 1 x 0 x
0 0 0 0 0 0 0 0 x 0 x
0 0 0 0 0 0 0 1 x 0 x
0 0 0 0 0 0 0 0 x 0 x
0 0 0 0 0 0 0 1 x 0 x
0 0 0 0 0 0 0 0 x 0 x
0 0 0 0 0 0 0 1 x 0 x
0 0 0 0 0 0 0 0 x 0 x
0 0 0 0 0 0 0 1 x 0 x
0 0 0 0 0 0 0 0 x 0 x
0 0 0 0 0 0 0 1 x 0 x
0 0 0 0 0 0 0 0 x 0 x
0 0 0 0 0 0 0 1 x 0 x
0 0 0 0 0 0 0 0 x 0 x
0 0 0 0 0 0 0 1 x 0 x
0 0 0 0 0 0 0 0 x 0 x
0 0 0 0 0 0 0 1 x 0 x
0 0 0 0 0 0 0 0 x 0 x
0 0 0 0 0 0 0 1 x 0 x
0 0 0 0 0 0 0 0 x 0 x
0 0 0 0 0 0 0 1 x 0 x
0 0 0 0 0 0 0 0 x 0 x
0 0 0 0 0 0 0 1 x 0 x
0 0 0 0 0 0 0 0 x 0 x
0 0 0 0 0 0 0 1 x 0 x
0 0 0 0 0 0 0 0 x 0 x
0 0 0 0 0 0 0 1 x 0 x
0 0 0 0 0 0 0 0 x 0 x
0 0 0 0 0 0 0 1 x 0 x
0 0 0 0 0 0 0 0 x 0 x
0 0 0 0 0 0 0 1 x 0 x
0 0 0 0 0 0 0 0 x 0 x
0 0 0 0 0 0 0 1 x 0 x
0 0 0 0 0 0 0 0 x 0 x
0 0 0 0 0 0 0 1 x 0 x
0 0 0 0 0 0 0 0 x 0 x
0 0 0 0 0 0 0 1 x 0 x
0 0 0 0 0 0 0 0 x 0 x
0 0 0 0 0 0 0 1 x 0 x
0 0 0 0 0 0 0 0 x 0 x
0 0 0 0 0 0 0 1 x 0 x
0 0 0 0 0 0 0 0 x 0 x
0 0 0 0 0 0 0 1 x 0 x
0 0 0 0 0 0 0 0 x 0 x
0 0 0 0 0 0 0 1 x 0 x
0 0 0 0 0 0 0 0 x 0 x
0 0 0 0 0 0 0 1 x 0 x
0 0 0 0 0 0 0 0 x 0 x
0 0 0 0 0 0 0 1 x 0 x
0 0 0 0 0 0 0 0 x 0 x
0 0 0 0 0 0 0 1 x 0 x
0 0 0 0 0 0 0 0 x 0 x
0 0 0 0 0 0 0 1 x 0 x
0 0 0 0 0 0 0 0 x 0 x
0 0 0 0 0 0 0 1 x 0 x
0 0 0 0 0 0 0 0 x 0 x
0 0 0 0 0 0 0 1 x 0 x
0 0 0 0 0 0 0 0 x 0 x
0 0 0 0 0 0 0 1 x 0 x
0 0 0 0 0 0 0 0 x 0 x
0 0 0 0 0 0 0 1 x 0 x
0 0 0 0 0 0 0 0 x 0 x
0 0 0 0 0 0 0 1 x 0 x
0 0 0 0 0 0 0 0 x 0 x
0 0 0 0 0 0 0 1 x 0 x
0 0 0 0 0 0 0 0 x 0 x
0 0 0 0 0 0 0 1 x 0 x
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*/

/* Test case 09_P09T01:
M N progIn reset progLoad start result clk valid done output
0 0 0 0 0 0 0 0 x x x
0 0 0 0 0 0 0 1 x x x
0 0 0 1 0 0 0 0 x x x
0 0 0 1 0 0 0 1 0 0 x
0 0 0 0 0 0 0 0 0 x x
0 0 0 0 0 0 0 1 0 x x
0 0 0 0 0 0 0 0 0 x x
0 0 0 0 0 0 0 1 0 x x
0 0 0 0 0 0 0 0 0 x x
0 0 0 0 0 0 0 1 0 x x
0 0 0 0 0 0 0 0 0 x x
0 0 0 0 0 0 0 1 0 x x
0 0 0 0 0 0 0 0 0 x x
0 0 0 0 0 0 0 1 0 x x
0 0 0 0 0 0 0 0 0 x x
0 0 0 0 0 0 0 1 0 x x
0 0 0 0 0 0 0 0 0 x x
0 0 0 0 0 0 0 1 0 x x
0 0 0 0 0 0 0 0 0 x x
0 0 0 0 0 0 0 1 0 x x
0 0 0 0 0 0 0 0 0 x x
0 0 0 0 0 0 0 1 0 x x
0 0 0 0 0 0 0 0 0 x x
0 0 0 0 0 0 0 1 0 x x
0 0 0 0 0 0 0 0 0 x x
0 0 0 0 0 0 0 1 0 x x
0 0 0 0 0 0 0 0 0 x x
0 0 0 0 0 0 0 1 0 x x
0 0 0 0 0 0 0 0 0 x x
0 0 0 0 0 0 0 1 0 x x
0 0 0 0 0 0 0 0 0 x x
0 0 0 0 0 0 0 1 0 x x
0 0 0 0 0 0 0 0 0 x x
0 0 0 0 0 0 0 1 0 x x
0 0 0 0 0 0 0 0 0 x x
0 0 0 0 0 0 0 1 0 x x
0 0 0 0 0 0 0 0 0 x x
0 0 0 0 0 0 0 1 0 x x
0 0 0 0 0 0 0 0 0 x x
0 0 0 0 0 0 0 1 0 x x
0 0 0 0 0 0 0 0 0 x x
0 0 0 0 0 0 0 1 0 x x
0 0 0 0 0 0 0 0 0 x x
0 0 0 0 0 0 0 1 0 x x
0 0 458 0 1 0 0 0 0 x x
0 0 458 0 1 0 0 1 0 x x
0 0 607 0 1 0 0 0 0 x x
0 0 607 0 1 0 0 1 0 x x
0 0 10240 0 1 0 0 0 0 x x
0 0 10240 0 1 0 0 1 0 x x
0 0 4352 0 1 0 0 0 0 x x
0 0 4352 0 1 0 0 1 0 x x
0 0 458 0 1 0 0 0 0 x x
0 0 458 0 1 0 0 1 0 x x
0 0 10496 0 1 0 0 0 0 x x
0 0 10496 0 1 0 0 1 0 x x
0 0 4353 0 1 0 0 0 0 x x
0 0 4353 0 1 0 0 1 0 x x
0 0 458 0 1 0 0 0 0 x x
0 0 458 0 1 0 0 1 0 x x
0 0 10752 0 1 0 0 0 0 x x
0 0 10752 0 1 0 0 1 0 x x
0 0 4354 0 1 0 0 0 0 x x
0 0 4354 0 1 0 0 1 0 x x
0 0 458 0 1 0 0 0 0 x x
0 0 458 0 1 0 0 1 0 x x
0 0 11008 0 1 0 0 0 0 x x
0 0 11008 0 1 0 0 1 0 x x
0 0 4355 0 1 0 0 0 0 x x
0 0 4355 0 1 0 0 1 0 x x
0 0 16128 0 1 0 0 0 0 x x
0 0 16128 0 1 0 0 1 0 x x
0 0 0 0 0 1 0 0 x x x
0 0 0 0 0 1 0 1 x 0 x
0 0 0 0 0 0 0 0 x 0 x
0 0 0 0 0 0 0 1 x 0 x
0 0 0 0 0 0 0 0 x 0 x
0 0 0 0 0 0 0 1 x 0 x
0 0 0 0 0 0 0 0 x 0 x
0 0 0 0 0 0 0 1 x 0 x
0 0 0 0 0 0 0 0 x 0 x
0 0 0 0 0 0 0 1 x 0 x
0 0 0 0 0 0 0 0 x 0 x
0 0 0 0 0 0 0 1 x 0 x
0 0 0 0 0 0 0 0 x 0 x
0 0 0 0 0 0 0 1 x 0 x
0 0 0 0 0 0 0 0 x 0 x
0 0 0 0 0 0 0 1 x 0 x
0 0 0 0 0 0 0 0 x 0 x
0 0 0 0 0 0 0 1 x 0 x
0 0 0 0 0 0 0 0 x 0 x
0 0 0 0 0 0 0 1 x 0 x
0 0 0 0 0 0 0 0 x 0 x
0 0 0 0 0 0 0 1 x 0 x
0 0 0 0 0 0 0 0 x 0 x
0 0 0 0 0 0 0 1 x 0 x
0 0 0 0 0 0 0 0 x 0 x
0 0 0 0 0 0 0 1 x 0 x
0 0 0 0 0 0 0 0 x 0 x
0 0 0 0 0 0 0 1 x 0 x
0 0 0 0 0 0 0 0 x 0 x
0 0 0 0 0 0 0 1 x 0 x
0 0 0 0 0 0 0 0 x 0 x
0 0 0 0 0 0 0 1 x 0 x
0 0 0 0 0 0 0 0 x 0 x
0 0 0 0 0 0 0 1 x 0 x
0 0 0 0 0 0 0 0 x 0 x
0 0 0 0 0 0 0 1 x 0 x
0 0 0 0 0 0 0 0 x 0 x
0 0 0 0 0 0 0 1 x 0 x
0 0 0 0 0 0 0 0 x 0 x
0 0 0 0 0 0 0 1 x 0 x
0 0 0 0 0 0 0 0 x 0 x
0 0 0 0 0 0 0 1 x 0 x
0 0 0 0 0 0 0 0 x 0 x
0 0 0 0 0 0 0 1 x 0 x
0 0 0 0 0 0 0 0 x 0 x
0 0 0 0 0 0 0 1 x 0 x
0 0 0 0 0 0 0 0 x 0 x
0 0 0 0 0 0 0 1 x 0 x
0 0 0 0 0 0 0 0 x 0 x
0 0 0 0 0 0 0 1 x 0 x
0 0 0 0 0 0 0 0 x 0 x
0 0 0 0 0 0 0 1 x 0 x
0 0 0 0 0 0 0 0 x 0 x
0 0 0 0 0 0 0 1 x 0 x
0 0 0 0 0 0 0 0 x 0 x
0 0 0 0 0 0 0 1 x 0 x
0 0 0 0 0 0 0 0 x 0 x
0 0 0 0 0 0 0 1 x 0 x
0 0 0 0 0 0 0 0 x 0 x
0 0 0 0 0 0 0 1 x 0 x
0 0 0 0 0 0 0 0 x 0 x
0 0 0 0 0 0 0 1 x 0 x
0 0 0 0 0 0 0 0 x 0 x
0 0 0 0 0 0 0 1 x 0 x
0 0 0 0 0 0 0 0 x 0 x
0 0 0 0 0 0 0 1 x 0 x
0 0 0 0 0 0 0 0 x 0 x
0 0 0 0 0 0 0 1 x 0 x
0 0 0 0 0 0 0 0 x 0 x
0 0 0 0 0 0 0 1 x 0 x
0 0 0 0 0 0 0 0 x 0 x
0 0 0 0 0 0 0 1 x 0 x
0 0 0 0 0 0 0 0 x 0 x
0 0 0 0 0 0 0 1 x 0 x
0 0 0 0 0 0 0 0 x 0 x
0 0 0 0 0 0 0 1 x 0 x
0 0 0 0 0 0 0 0 x 0 x
0 0 0 0 0 0 0 1 x 0 x
0 0 0 0 0 0 0 0 x 0 x
0 0 0 0 0 0 0 1 x 0 x
0 0 0 0 0 0 0 0 x 0 x
0 0 0 0 0 0 0 1 x 0 x
0 0 0 0 0 0 0 0 x 0 x
0 0 0 0 0 0 0 1 x 0 x
0 0 0 0 0 0 0 0 x 0 x
0 0 0 0 0 0 0 1 x 0 x
0 0 0 0 0 0 0 0 x 0 x
0 0 0 0 0 0 0 1 x 0 x
0 0 0 0 0 0 0 0 x 0 x
0 0 0 0 0 0 0 1 x 0 x
0 0 0 0 0 0 0 0 x 0 x
0 0 0 0 0 0 0 1 x 0 x
0 0 0 0 0 0 0 0 x 0 x
0 0 0 0 0 0 0 1 x 0 x
0 0 0 0 0 0 0 0 x 0 x
0 0 0 0 0 0 0 1 x 0 x
0 0 0 0 0 0 0 0 x 0 x
0 0 0 0 0 0 0 1 x 0 x
0 0 0 0 0 0 0 0 x 0 x
0 0 0 0 0 0 0 1 x 0 x
0 0 0 0 0 0 0 0 x 0 x
0 0 0 0 0 0 0 1 x 0 x
0 0 0 0 0 0 0 0 x 0 x
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*/

/* Test case 06_P06T01:
M N progIn reset progLoad start result clk valid done output
0 0 0 0 0 0 0 0 x x x
0 0 0 0 0 0 0 1 x x x
0 0 0 1 0 0 0 0 x x x
0 0 0 1 0 0 0 1 0 0 x
0 0 0 0 0 0 0 0 0 x x
0 0 0 0 0 0 0 1 0 x x
0 0 0 0 0 0 0 0 0 x x
0 0 0 0 0 0 0 1 0 x x
0 0 0 0 0 0 0 0 0 x x
0 0 0 0 0 0 0 1 0 x x
0 0 0 0 0 0 0 0 0 x x
0 0 0 0 0 0 0 1 0 x x
0 0 0 0 0 0 0 0 0 x x
0 0 0 0 0 0 0 1 0 x x
0 0 0 0 0 0 0 0 0 x x
0 0 0 0 0 0 0 1 0 x x
0 0 0 0 0 0 0 0 0 x x
0 0 0 0 0 0 0 1 0 x x
0 0 0 0 0 0 0 0 0 x x
0 0 0 0 0 0 0 1 0 x x
0 0 0 0 0 0 0 0 0 x x
0 0 0 0 0 0 0 1 0 x x
0 0 0 0 0 0 0 0 0 x x
0 0 0 0 0 0 0 1 0 x x
0 0 0 0 0 0 0 0 0 x x
0 0 0 0 0 0 0 1 0 x x
0 0 0 0 0 0 0 0 0 x x
0 0 0 0 0 0 0 1 0 x x
0 0 0 0 0 0 0 0 0 x x
0 0 0 0 0 0 0 1 0 x x
0 0 0 0 0 0 0 0 0 x x
0 0 0 0 0 0 0 1 0 x x
0 0 0 0 0 0 0 0 0 x x
0 0 0 0 0 0 0 1 0 x x
0 0 0 0 0 0 0 0 0 x x
0 0 0 0 0 0 0 1 0 x x
0 0 0 0 0 0 0 0 0 x x
0 0 0 0 0 0 0 1 0 x x
0 0 0 0 0 0 0 0 0 x x
0 0 0 0 0 0 0 1 0 x x
0 0 0 0 0 0 0 0 0 x x
0 0 0 0 0 0 0 1 0 x x
0 0 0 0 0 0 0 0 0 x x
0 0 0 0 0 0 0 1 0 x x
0 0 3072 0 1 0 0 0 0 x x
0 0 3072 0 1 0 0 1 0 x x
0 0 3328 0 1 0 0 0 0 x x
0 0 3328 0 1 0 0 1 0 x x
0 0 2048 0 1 0 0 0 0 x x
0 0 2048 0 1 0 0 1 0 x x
0 0 4352 0 1 0 0 0 0 x x
0 0 4352 0 1 0 0 1 0 x x
0 0 2304 0 1 0 0 0 0 x x
0 0 2304 0 1 0 0 1 0 x x
0 0 4353 0 1 0 0 0 0 x x
0 0 4353 0 1 0 0 1 0 x x
0 0 2048 0 1 0 0 0 0 x x
0 0 2048 0 1 0 0 1 0 x x
0 0 1280 0 1 0 0 0 0 x x
0 0 1280 0 1 0 0 1 0 x x
0 0 2304 0 1 0 0 0 0 x x
0 0 2304 0 1 0 0 1 0 x x
0 0 8192 0 1 0 0 0 0 x x
0 0 8192 0 1 0 0 1 0 x x
0 0 4354 0 1 0 0 0 0 x x
0 0 4354 0 1 0 0 1 0 x x
0 0 16128 0 1 0 0 0 0 x x
0 0 16128 0 1 0 0 1 0 x x
18 52 0 0 0 1 0 0 x x x
18 52 0 0 0 1 0 1 x 0 x
18 52 0 0 0 0 0 0 x 0 x
18 52 0 0 0 0 0 1 x 0 x
18 52 0 0 0 0 0 0 x 0 x
18 52 0 0 0 0 0 1 x 0 x
18 52 0 0 0 0 0 0 x 0 x
18 52 0 0 0 0 0 1 x 0 x
18 52 0 0 0 0 0 0 x 0 x
18 52 0 0 0 0 0 1 x 0 x
18 52 0 0 0 0 0 0 x 0 x
18 52 0 0 0 0 0 1 x 0 x
18 52 0 0 0 0 0 0 x 0 x
18 52 0 0 0 0 0 1 x 0 x
18 52 0 0 0 0 0 0 x 0 x
18 52 0 0 0 0 0 1 x 0 x
18 52 0 0 0 0 0 0 x 0 x
18 52 0 0 0 0 0 1 x 0 x
18 52 0 0 0 0 0 0 x 0 x
18 52 0 0 0 0 0 1 x 0 x
18 52 0 0 0 0 0 0 x 0 x
18 52 0 0 0 0 0 1 x 0 x
18 52 0 0 0 0 0 0 x 0 x
18 52 0 0 0 0 0 1 x 0 x
18 52 0 0 0 0 0 0 x 0 x
18 52 0 0 0 0 0 1 x 0 x
18 52 0 0 0 0 0 0 x 0 x
18 52 0 0 0 0 0 1 x 0 x
18 52 0 0 0 0 0 0 x 0 x
18 52 0 0 0 0 0 1 x 0 x
18 52 0 0 0 0 0 0 x 0 x
18 52 0 0 0 0 0 1 x 0 x
18 52 0 0 0 0 0 0 x 0 x
18 52 0 0 0 0 0 1 x 0 x
18 52 0 0 0 0 0 0 x 0 x
18 52 0 0 0 0 0 1 x 0 x
18 52 0 0 0 0 0 0 x 0 x
18 52 0 0 0 0 0 1 x 0 x
18 52 0 0 0 0 0 0 x 0 x
18 52 0 0 0 0 0 1 x 0 x
18 52 0 0 0 0 0 0 x 0 x
18 52 0 0 0 0 0 1 x 0 x
18 52 0 0 0 0 0 0 x 0 x
18 52 0 0 0 0 0 1 x 0 x
18 52 0 0 0 0 0 0 x 0 x
18 52 0 0 0 0 0 1 x 0 x
18 52 0 0 0 0 0 0 x 0 x
18 52 0 0 0 0 0 1 x 0 x
18 52 0 0 0 0 0 0 x 0 x
18 52 0 0 0 0 0 1 x 0 x
18 52 0 0 0 0 0 0 x 0 x
18 52 0 0 0 0 0 1 x 0 x
18 52 0 0 0 0 0 0 x 0 x
18 52 0 0 0 0 0 1 x 0 x
18 52 0 0 0 0 0 0 x 0 x
18 52 0 0 0 0 0 1 x 0 x
18 52 0 0 0 0 0 0 x 0 x
18 52 0 0 0 0 0 1 x 0 x
18 52 0 0 0 0 0 0 x 0 x
18 52 0 0 0 0 0 1 x 0 x
18 52 0 0 0 0 0 0 x 0 x
18 52 0 0 0 0 0 1 x 0 x
18 52 0 0 0 0 0 0 x 0 x
18 52 0 0 0 0 0 1 x 0 x
18 52 0 0 0 0 0 0 x 0 x
18 52 0 0 0 0 0 1 x 0 x
18 52 0 0 0 0 0 0 x 0 x
18 52 0 0 0 0 0 1 x 0 x
18 52 0 0 0 0 0 0 x 0 x
18 52 0 0 0 0 0 1 x 0 x
18 52 0 0 0 0 0 0 x 0 x
18 52 0 0 0 0 0 1 x 0 x
18 52 0 0 0 0 0 0 x 0 x
18 52 0 0 0 0 0 1 x 0 x
18 52 0 0 0 0 0 0 x 0 x
18 52 0 0 0 0 0 1 x 0 x
18 52 0 0 0 0 0 0 x 0 x
18 52 0 0 0 0 0 1 x 0 x
18 52 0 0 0 0 0 0 x 0 x
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*/

/* Test case 03_P03T01:
M N progIn reset progLoad start result clk valid done output
0 0 0 0 0 0 0 0 x x x
0 0 0 0 0 0 0 1 x x x
0 0 0 1 0 0 0 0 x x x
0 0 0 1 0 0 0 1 0 0 x
0 0 0 0 0 0 0 0 0 x x
0 0 0 0 0 0 0 1 0 x x
0 0 0 0 0 0 0 0 0 x x
0 0 0 0 0 0 0 1 0 x x
0 0 0 0 0 0 0 0 0 x x
0 0 0 0 0 0 0 1 0 x x
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*/

/* Test case 24_P11T02:
M N progIn reset progLoad start result clk valid done output
0 0 0 0 0 0 0 C x x x
0 0 0 1 0 0 0 C 0 0 x
repeat(20) 0 0 0 0 0 0 0 C 0 x x
0 0 256 0 1 0 0 C 0 x x
0 0 1536 0 1 0 0 C 0 x x
0 0 259 0 1 0 0 C 0 x x
0 0 1792 0 1 0 0 C 0 x x
0 0 2304 0 1 0 0 C 0 x x
0 0 6144 0 1 0 0 C 0 x x
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*/

/* Test case 21_P08T02:
M N progIn reset progLoad start result clk valid done output
0 0 0 0 0 0 0 C x x x
0 0 0 1 0 0 0 C 0 0 x
repeat(20) 0 0 0 0 0 0 0 C 0 x x
0 0 456 0 1 0 0 C 0 x x
0 0 519 0 1 0 0 C 0 x x
0 0 9216 0 1 0 0 C 0 x x
0 0 4352 0 1 0 0 C 0 x x
0 0 456 0 1 0 0 C 0 x x
0 0 9472 0 1 0 0 C 0 x x
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*/

/* Test case 18_P05T02:
M N progIn reset progLoad start result clk valid done output
0 0 0 0 0 0 0 C x x x
0 0 0 1 0 0 0 C 0 0 x
repeat(20) 0 0 0 0 0 0 0 C 0 x x
0 0 260 0 1 0 0 C 0 x x
0 0 516 0 1 0 0 C 0 x x
0 0 14336 0 1 0 0 C 0 x x
0 0 14592 0 1 0 0 C 0 x x
0 0 12569 0 1 0 0 C 0 x x
0 0 257 0 1 0 0 C 0 x x
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*/

/* Test case 15_P02T02:
M N progIn reset progLoad start result clk valid done output
0 0 0 0 0 0 0 C x x x
0 0 0 1 0 0 0 C 0 0 x
repeat(20) 0 0 0 0 0 0 0 C 0 x x
0 0 496 0 1 0 0 C 0 x x
0 0 517 0 1 0 0 C 0 x x
0 0 14336 0 1 0 0 C 0 x x
0 0 13061 0 1 0 0 C 0 x x
0 0 256 0 1 0 0 C 0 x x
0 0 4352 0 1 0 0 C 0 x x
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*/

/* Test case 11_P11T01:
M N progIn reset progLoad start result clk valid done output
0 0 0 0 0 0 0 0 x x x
0 0 0 0 0 0 0 1 x x x
0 0 0 1 0 0 0 0 x x x
0 0 0 1 0 0 0 1 0 0 x
0 0 0 0 0 0 0 0 0 x x
0 0 0 0 0 0 0 1 0 x x
0 0 0 0 0 0 0 0 0 x x
0 0 0 0 0 0 0 1 0 x x
0 0 0 0 0 0 0 0 0 x x
0 0 0 0 0 0 0 1 0 x x
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*/

/* Test case 08_P08T01:
M N progIn reset progLoad start result clk valid done output
0 0 0 0 0 0 0 0 x x x
0 0 0 0 0 0 0 1 x x x
0 0 0 1 0 0 0 0 x x x
0 0 0 1 0 0 0 1 0 0 x
0 0 0 0 0 0 0 0 0 x x
0 0 0 0 0 0 0 1 0 x x
0 0 0 0 0 0 0 0 0 x x
0 0 0 0 0 0 0 1 0 x x
0 0 0 0 0 0 0 0 0 x x
0 0 0 0 0 0 0 1 0 x x
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*/

/* Test case 05_P05T01:
M N progIn reset progLoad start result clk valid done output
0 0 0 0 0 0 0 0 x x x
0 0 0 0 0 0 0 1 x x x
0 0 0 1 0 0 0 0 x x x
0 0 0 1 0 0 0 1 0 0 x
0 0 0 0 0 0 0 0 0 x x
0 0 0 0 0 0 0 1 0 x x
0 0 0 0 0 0 0 0 0 x x
0 0 0 0 0 0 0 1 0 x x
0 0 0 0 0 0 0 0 0 x x
0 0 0 0 0 0 0 1 0 x x
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*/

/* Test case 02_P02T01:
M N progIn reset progLoad start result clk valid done output
0 0 0 0 0 0 0 0 x x x
0 0 0 0 0 0 0 1 x x x
0 0 0 1 0 0 0 0 x x x
0 0 0 1 0 0 0 1 0 0 x
0 0 0 0 0 0 0 0 0 x x
0 0 0 0 0 0 0 1 0 x x
0 0 0 0 0 0 0 0 0 x x
0 0 0 0 0 0 0 1 0 x x
0 0 0 0 0 0 0 0 0 x x
0 0 0 0 0 0 0 1 0 x x
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*/

/* Test case 26_P13T02:
M N progIn reset progLoad start result clk valid done output
0 0 0 0 0 0 0 C x x x
0 0 0 1 0 0 0 C 0 0 x
repeat(20) 0 0 0 0 0 0 0 C 0 x x
0 0 280 0 1 0 0 C 0 x x
0 0 15616 0 1 0 0 C 0 x x
0 0 4106 0 1 0 0 C 0 x x
0 0 4352 0 1 0 0 C 0 x x
0 0 4107 0 1 0 0 C 0 x x
0 0 4353 0 1 0 0 C 0 x x
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*/

/* Test case 23_P10T02:
M N progIn reset progLoad start result clk valid done output
0 0 0 0 0 0 0 C x x x
0 0 0 1 0 0 0 C 0 0 x
repeat(20) 0 0 0 0 0 0 0 C 0 x x
0 0 264 0 1 0 0 C 0 x x
0 0 1792 0 1 0 0 C 0 x x
0 0 273 0 1 0 0 C 0 x x
0 0 6144 0 1 0 0 C 0 x x
0 0 529 0 1 0 0 C 0 x x
0 0 8192 0 1 0 0 C 0 x x
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*/

/* Test case 20_P07T02:
M N progIn reset progLoad start result clk valid done output
0 0 0 0 0 0 0 C x x x
0 0 0 1 0 0 0 C 0 0 x
repeat(20) 0 0 0 0 0 0 0 C 0 x x
0 0 320 0 1 0 0 C 0 x x
0 0 1536 0 1 0 0 C 0 x x
0 0 264 0 1 0 0 C 0 x x
0 0 1792 0 1 0 0 C 0 x x
0 0 259 0 1 0 0 C 0 x x
0 0 5376 0 1 0 0 C 0 x x
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*/

/* Test case 17_P04T02:
M N progIn reset progLoad start result clk valid done output
0 0 0 0 0 0 0 C x x x
0 0 0 1 0 0 0 C 0 0 x
repeat(20) 0 0 0 0 0 0 0 C 0 x x
0 0 256 0 1 0 0 C 0 x x
0 0 14592 0 1 0 0 C 0 x x
0 0 256 0 1 0 0 C 0 x x
0 0 12549 0 1 0 0 C 0 x x
0 0 12294 0 1 0 0 C 0 x x
0 0 257 0 1 0 0 C 0 x x
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*/

/* Test case 14_P01T02:
M N progIn reset progLoad start result clk valid done output
0 0 0 0 0 0 0 C x x x
0 0 0 1 0 0 0 C 0 0 x
repeat(20) 0 0 0 0 0 0 0 C 0 x x
0 0 346 0 1 0 0 C 0 x x
0 0 4352 0 1 0 0 C 0 x x
0 0 677 0 1 0 0 C 0 x x
0 0 1024 0 1 0 0 C 0 x x
0 0 4367 0 1 0 0 C 0 x x
0 0 375 0 1 0 0 C 0 x x
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*/

/* Test case 13_P13T01:
M N progIn reset progLoad start result clk valid done output
0 0 0 0 0 0 0 0 x x x
0 0 0 0 0 0 0 1 x x x
0 0 0 1 0 0 0 0 x x x
0 0 0 1 0 0 0 1 0 0 x
0 0 0 0 0 0 0 0 0 x x
0 0 0 0 0 0 0 1 0 x x
0 0 0 0 0 0 0 0 0 x x
0 0 0 0 0 0 0 1 0 x x
0 0 0 0 0 0 0 0 0 x x
0 0 0 0 0 0 0 1 0 x x
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*/

/* Test case 10_P10T01:
M N progIn reset progLoad start result clk valid done output
0 0 0 0 0 0 0 0 x x x
0 0 0 0 0 0 0 1 x x x
0 0 0 1 0 0 0 0 x x x
0 0 0 1 0 0 0 1 0 0 x
0 0 0 0 0 0 0 0 0 x x
0 0 0 0 0 0 0 1 0 x x
0 0 0 0 0 0 0 0 0 x x
0 0 0 0 0 0 0 1 0 x x
0 0 0 0 0 0 0 0 0 x x
0 0 0 0 0 0 0 1 0 x x
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*/

/* Test case 07_P07T01:
M N progIn reset progLoad start result clk valid done output
0 0 0 0 0 0 0 0 x x x
0 0 0 0 0 0 0 1 x x x
0 0 0 1 0 0 0 0 x x x
0 0 0 1 0 0 0 1 0 0 x
0 0 0 0 0 0 0 0 0 x x
0 0 0 0 0 0 0 1 0 x x
0 0 0 0 0 0 0 0 0 x x
0 0 0 0 0 0 0 1 0 x x
0 0 0 0 0 0 0 0 0 x x
0 0 0 0 0 0 0 1 0 x x
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*/

/* Test case 04_P04T01:
M N progIn reset progLoad start result clk valid done output
0 0 0 0 0 0 0 0 x x x
0 0 0 0 0 0 0 1 x x x
0 0 0 1 0 0 0 0 x x x
0 0 0 1 0 0 0 1 0 0 x
0 0 0 0 0 0 0 0 0 x x
0 0 0 0 0 0 0 1 0 x x
0 0 0 0 0 0 0 0 0 x x
0 0 0 0 0 0 0 1 0 x x
0 0 0 0 0 0 0 0 0 x x
0 0 0 0 0 0 0 1 0 x x
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*/

/* Test case 01_P01T01:
M N progIn reset progLoad start result clk valid done output
0 0 0 0 0 0 0 0 x x x
0 0 0 0 0 0 0 1 x x x
0 0 0 1 0 0 0 0 x x x
0 0 0 1 0 0 0 1 0 0 x
0 0 0 0 0 0 0 0 0 x x
0 0 0 0 0 0 0 1 0 x x
0 0 0 0 0 0 0 0 0 x x
0 0 0 0 0 0 0 1 0 x x
0 0 0 0 0 0 0 0 0 x x
0 0 0 0 0 0 0 1 0 x x
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*/
